# Fritzing sketch BehavioralBoxSchematic_Final (saved by Fritzing 0.9.10b)
circuit board: 8.46667cm x 5.64444cm
breadboards: 2

parts:
  A1 = Teensy 4.1
  A2 = Teensy 4.1
  Part2 = Audio FX Sound Board + 2x2W Amp
  Part3 = Adafruit MPR121 [part_number="Adafruit #1982"]
  R1 = Resistor [tolerance=±5% resistance=10000 package="0805 [SMD]"]
  Q2 = PNP-Transistor [package="TO92 [THT]"]
  D1 = Diode [package=diode-1n4148]
  Part4 = NeoPixel NeoMatrix 8x8 [part_number=1487]

nets:
  N1: A1.Pin_12, A1.Pin_50, A1.Pin_63, Part4.GND
  N2: A1.Pin_13, Part2.TX
  N3: A1.Pin_14, Part2.RX
  N4: A1.Pin_17, R1.Pin_0
  N5: A1.Pin_21, Part4.IN
  N6: A1.Pin_26, A1.Pin_37, A1.Pin_62, Part2.VIN
  N7: A1.Pin_32, A2.Pin_32
  N8: A1.Pin_33, A2.Pin_33
  N9: A1.Pin_34, A2.Pin_34
  N10: A1.Pin_35, A2.Pin_35
  N11: A1.Pin_41, A2.Pin_41
  N12: A1.Pin_42, A2.Pin_42
  N13: A1.Pin_43, A2.Pin_43
  N14: A1.Pin_44, A2.Pin_44
  N15: A1.Pin_57, Part2.RST
  N16: A1.Pin_64, D1.C, Part4.VDD
  N17: A2.Pin_12, A2.Pin_38, A2.Pin_50, A2.Pin_63, Part3.GND
  N18: A2.Pin_26, A2.Pin_37, A2.Pin_62, Part3.VCC
  N19: A2.Pin_56, Part3.SDA
  N20: A2.Pin_57, Part3.SCL
  N21: Part2.GND, Q2.E
  N22: R1.Pin_1, Q2.B

notes:
  Behavior Teensy
  Coordinate Teensy
  Soundboard
  Lick Sensor
  Line that connects to the lick spout
  Connects to Solenoid
  Light Array

custom parts:
  Teensy 4.1: The Teensy is a complete USB-based microcontoller development system, in a very small footprint, capable of implementing many types of projects. All programming is done via the USB port. No special programmer is needed, only a standard micro-USB cable and a PC or Macintosh with a USB port.
  Audio FX Sound Board + 2x2W Amp: The Adafruit Sound Board, the fastest way to add audio effects to a project!
  Adafruit MPR121: Add lots of touch sensors to your next microcontroller project with this easy-to-use 12-channel capacitive touch sensor breakout board, starring the MPR121. This chip can handle up to 12 individual touch pads. The MPR121 has support for only I2C, which can be implemented with nearly any microcontroller. You can select one of 4 addresses with the ADDR pin, for a total of 48 capacitive touch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
  NeoPixel NeoMatrix 8x8: Put on your sunglasses before wiring up this LED matrix - 64 eye-blistering RGB LEDs adorn the NeoMatrix for a blast of configurable color. Arranged in an 8x8 matrix, each pixel is individually addressable. Only one microcontroller pin is required to control all the LEDs, and you get 24 bit color for each LED.
