# Fritzing sketch BehaviorBoxCircuitfzz (saved by Fritzing 0.9.10b)
circuit board: 15.3442cm x 6.21743cm
breadboards: 3

parts:
  A1 = Teensy 4.1
  A2 = Teensy 4.1
  Part1 = Audio FX Sound Board + 2x2W Amp
  Q3 = TIP120 Hi-Current Darlington Transistor
  R3 = Resistor [tolerance=±1% power=0.25 resistance=1000 package=THT]
  R4 = Resistor [tolerance=±5% power=0.25 resistance=1000 package=THT]
  L3 = Solenoid
  D3 = Rectifier Diode [part_number=1N4001 package="300 mil [THT]"]
  D4 = Rectifier Diode [part_number=1N4001 package="300 mil [THT]"]
  Q4 = TRANSISTOR_NPN [package=to-92-ammo]
  L4 = Solenoid
  U1 = JOYSTICK-PSP1000 [package=joystick-psp1000]
  LED1 = smd LED [color="Blue (505nm)" package="1206 [SMD]"]
  R5 = Resistor [tolerance=±5% power=0.25 resistance=220 package=THT]
  U2 = BNC socket [package=bnc]
  U3 = BNC socket [package=bnc]
  U4 = BNC socket [package=bnc]
  U5 = BNC socket [package=bnc]

nets:
  GND: A1.Pin_12, A1.Pin_38, A1.Pin_50, A1.Pin_63, A1.Pin_64, Part1.GND, Part1.UG, Q3.COLLECTOR, Q3.EMITTER, L3.pin1, L3.pin2, D3.cathode, D4.cathode, D4.anode, Q4.C, L4.pin2, LED1.cathode, R5.Pin_1, U4.GND, U5.GND
  N1: A1.Pin_13, Part1.TX
  N2: A1.Pin_14, Part1.RX
  N3: A1.Pin_17, R3.Pin_0
  N4: A1.Pin_20, A2.Pin_21
  N5: A1.Pin_21, A2.Pin_20
  N6: A1.Pin_23, R4.Pin_0
  N7: A1.Pin_26, A1.Pin_37, A1.Pin_62, Part1.VIN
  N8: A1.Pin_32, A2.Pin_32
  N9: A1.Pin_33, A2.Pin_33
  N10: A1.Pin_34, A2.Pin_34
  N11: A1.Pin_35, A2.Pin_35
  N12: A1.Pin_41, A2.Pin_41
  N13: A1.Pin_42, A2.Pin_42
  N14: A1.Pin_43, A2.Pin_43
  N15: A1.Pin_46, U5.OUT
  N16: A1.Pin_47, U4.OUT
  N17: A1.Pin_57, Part1.RST
  GND_2: A2.Pin_12, A2.Pin_38, A2.Pin_50, A2.Pin_63, U1.GND, U2.GND, U3.GND
  N18: A2.Pin_13, LED1.anode, R5.Pin_0
  N19: A2.Pin_26, A2.Pin_62, U1.VCC
  N20: A2.Pin_52, U1.X, U2.OUT
  N21: A2.Pin_53, U1.Y, U3.OUT
  N22: Q3.BASE, R4.Pin_1
  N23: R3.Pin_1, Q4.B
  N24: D3.anode, Q4.E, L4.pin1

notes:
  Add BNC Connectors for:
  Solenoid
  Soundboard (digitalWrite High)
  X Coords
  Y Coords
  Add Pins for digitalRead + Write
  X Coordinate BNC
  Y Coordinate BNC
  Soundboard BNC
  Solenoid BNC

custom parts:
  Teensy 4.1: The Teensy is a complete USB-based microcontoller development system, in a very small footprint, capable of implementing many types of projects. All programming is done via the USB port. No special programmer is needed, only a standard micro-USB cable and a PC or Macintosh with a USB port.
  Audio FX Sound Board + 2x2W Amp: The Adafruit Sound Board, the fastest way to add audio effects to a project!
